// Logisim project control-logic.circ as structural Verilog: 1 circuit, main circuit control_logic
module control_logic (
  input  [31:0] Instruction,
  input  BrEq,
  input  BrLt,
  output PCSel,
  output RegWEn,
  output [2:0] ImmSel,
  output BrUn,
  output ASel,
  output BSel,
  output [3:0] ALUSel,
  output MemWEn,
  output [1:0] WBSel
);

  wire and_1_out, and_2_out, and_3_out, and_4_out, and_5_out, and_6_out, comparator_1_eq, comparator_2_eq,
       comparator_3_eq, comparator_4_eq, comparator_5_eq, comparator_6_eq, comparator_7_eq, comparator_8_eq,
       comparator_9_eq, comparator_10_eq, comparator_11_eq, comparator_12_eq, comparator_13_eq,
       comparator_14_eq, comparator_15_eq, comparator_16_eq, comparator_17_eq, comparator_18_eq,
       comparator_19_eq, comparator_20_eq, not_1_out, not_2_out, not_3_out, or_1_out, or_2_out, or_3_out,
       or_4_out;
  wire [3:0] PriOut;
  wire [5:0] BType, I2Type, IType, multiplexer_1_out, multiplexer_2_out, multiplexer_3_out,
       multiplexer_4_out, ROMInput, RType, SType;
  wire [15:14] rom_1_data;

  Multiplexer #(.width(6)) multiplexer_1 (
    .in0(6'b010011), .in1(6'b010100), .out(multiplexer_1_out), .sel(Instruction[30]));
  Multiplexer #(.select(2), .width(6)) multiplexer_2 (
    .in0({6{1'b0}}), .in1(6'b000001), .in2(6'b000010), .out(multiplexer_2_out),
    .sel({Instruction[30], Instruction[25]}));  // open: in3
  Multiplexer #(.select(2), .width(6)) multiplexer_3 (
    .in0(6'b000011), .in1(6'b000100), .out(multiplexer_3_out), .sel({Instruction[30], Instruction[25]}));  // open: in2, in3
  Multiplexer #(.select(2), .width(6)) multiplexer_4 (
    .in0(6'b001000), .in2(6'b001001), .out(multiplexer_4_out), .sel({Instruction[30], Instruction[25]}));  // open: in1, in3
  ROM #(.addrWidth(6), .dataWidth(16)) rom_1 (
    .addr(ROMInput), .data({rom_1_data, WBSel, MemWEn, ALUSel, BSel, ASel, BrUn, ImmSel, RegWEn}));
  Multiplexer #(.select(3), .width(6)) multiplexer_5 (
    .in0(6'b001111), .in1(6'b010000), .in2(6'b010001), .in4(6'b010010), .in5(multiplexer_1_out),
    .in6(6'b010101), .in7(6'b010110), .out(IType), .sel(Instruction[14:12]));  // open: in3
  Comparator #(.width(7)) comparator_1 (.a(Instruction[6:0]), .b(7'b0010011), .eq(comparator_1_eq));  // open: gt, lt
  Comparator #(.width(7)) comparator_2 (.a(Instruction[6:0]), .b(7'b0110011), .eq(comparator_2_eq));  // open: gt, lt
  Comparator #(.width(7)) comparator_3 (.a(Instruction[6:0]), .b(7'b1100011), .eq(comparator_3_eq));  // open: gt, lt
  Comparator #(.width(7)) comparator_4 (.a(Instruction[6:0]), .b(7'b0000011), .eq(comparator_4_eq));  // open: gt, lt
  Comparator #(.width(7)) comparator_5 (.a(Instruction[6:0]), .b(7'b0100011), .eq(comparator_5_eq));  // open: gt, lt
  Comparator #(.width(7)) comparator_6 (.a(Instruction[6:0]), .b(7'b1101111), .eq(comparator_6_eq));  // open: gt, lt
  Comparator #(.width(7)) comparator_7 (.a(Instruction[6:0]), .b(7'b1100111), .eq(comparator_7_eq));  // open: gt, lt
  Comparator #(.width(7)) comparator_8 (.a(Instruction[6:0]), .b(7'b0010111), .eq(comparator_8_eq));  // open: gt, lt
  Comparator #(.width(7)) comparator_9 (.a(Instruction[6:0]), .b(7'b0110111), .eq(comparator_9_eq));  // open: gt, lt
  Multiplexer #(.select(3), .width(6)) multiplexer_6 (
    .in0(multiplexer_2_out), .in1(multiplexer_3_out), .in2(6'b000110), .in3(6'b000101), .in4(6'b000111),
    .in5(multiplexer_4_out), .in6(6'b001010), .in7(6'b001011), .out(RType), .sel(Instruction[14:12]));
  Multiplexer #(.select(3), .width(6)) multiplexer_7 (
    .in0(6'b011010), .in1(6'b011011), .in4(6'b011100), .in5(6'b011101), .in6(6'b011110), .in7(6'b011111),
    .out(BType), .sel(Instruction[14:12]));  // open: in2, in3
  Multiplexer #(.select(3), .width(6)) multiplexer_8 (
    .in0(6'b001100), .in1(6'b001101), .in2(6'b001110), .out(I2Type), .sel(Instruction[14:12]));  // open: in3, in4, in5, in6, in7
  Multiplexer #(.select(3), .width(6)) multiplexer_9 (
    .in0(6'b010111), .in1(6'b011000), .in2(6'b011001), .out(SType), .sel(Instruction[14:12]));  // open: in3, in4, in5, in6, in7
  Priority_Encoder #(.select_enc(4)) priority_encoder_1 (
    .in0(comparator_1_eq), .in1(comparator_2_eq), .in2(comparator_3_eq), .in3(comparator_4_eq),
    .in4(comparator_5_eq), .in5(comparator_6_eq), .in6(comparator_7_eq), .in7(comparator_8_eq),
    .in8(comparator_9_eq), .out(PriOut), .en_in(1'b1));  // open: in9, in10, in11, in12, in13, in14, in15, gs, en_out
  Multiplexer #(.select(4), .width(6)) multiplexer_10 (
    .in0(IType), .in1(RType), .in2(BType), .in3(I2Type), .in4(SType), .in5(6'b100010), .in6(6'b100011),
    .in7(6'b100000), .in8(6'b100001), .out(ROMInput), .sel(PriOut));  // open: in9, in10, in11, in12, in13, in14, in15
  Comparator #(.width(6)) comparator_10 (.a(BType), .b(6'b011010), .eq(comparator_10_eq));  // open: gt, lt
  not not_1 (not_1_out, BrEq);
  Comparator #(.width(6)) comparator_11 (.a(BType), .b(6'b011011), .eq(comparator_11_eq));  // open: gt, lt
  Comparator #(.width(6)) comparator_12 (.a(BType), .b(6'b011100), .eq(comparator_12_eq));  // open: gt, lt
  Comparator #(.width(6)) comparator_13 (.a(BType), .b(6'b011101), .eq(comparator_13_eq));  // open: gt, lt
  Comparator #(.width(6)) comparator_14 (.a(BType), .b(6'b011110), .eq(comparator_14_eq));  // open: gt, lt
  Comparator #(.width(6)) comparator_15 (.a(BType), .b(6'b011111), .eq(comparator_15_eq));  // open: gt, lt
  not not_2 (not_2_out, BrLt);
  not not_3 (not_3_out, BrLt);
  Comparator #(.width(7)) comparator_16 (.a(7'b1101111), .b(Instruction[6:0]), .eq(comparator_16_eq));  // open: gt, lt
  Comparator #(.width(7)) comparator_17 (.a(7'b1100111), .b(Instruction[6:0]), .eq(comparator_17_eq));  // open: gt, lt
  and and_1 (and_1_out, BrEq, comparator_10_eq);
  and and_2 (and_2_out, not_1_out, comparator_11_eq);
  and and_3 (and_3_out, BrLt, comparator_12_eq);
  and and_4 (and_4_out, not_2_out, comparator_13_eq);
  and and_5 (and_5_out, BrLt, comparator_14_eq);
  and and_6 (and_6_out, not_3_out, comparator_15_eq);
  or or_1 (or_1_out, comparator_16_eq, comparator_17_eq);
  or or_2 (or_2_out, and_1_out, and_2_out, and_3_out, and_4_out, and_5_out, and_6_out);
  or or_3 (or_3_out, or_2_out, or_1_out);
  Multiplexer multiplexer_11 (.in0(1'b0), .in1(or_3_out), .out(PCSel), .sel(or_4_out));
  or or_4 (or_4_out, comparator_18_eq, comparator_19_eq, comparator_20_eq);
  Comparator #(.width(7)) comparator_18 (.a(7'b1100011), .b(Instruction[6:0]), .eq(comparator_18_eq));  // open: gt, lt
  Comparator #(.width(7)) comparator_19 (.a(7'b1101111), .b(Instruction[6:0]), .eq(comparator_19_eq));  // open: gt, lt
  Comparator #(.width(7)) comparator_20 (.a(7'b1100111), .b(Instruction[6:0]), .eq(comparator_20_eq));  // open: gt, lt

  // Other names for the same wires on the sheet: opcode[6:0] = Instruction[6:0]; rd[4:0] = Instruction[11:7];
  //   func3[2:0] = Instruction[14:12]; rs1[4:0] = Instruction[19:15]; rs2[4:0] = Instruction[24:20];
  //   func7[6:0] = Instruction[31:25]

  // Notes on the sheet:
  //   INPUTS to your circuit
  //   IType
  //   RType
  //   BType
  //   I2Type
  //   SType
  //   U2Type
  //   JType
  //   Connect ROM Input here ->
  //   I:0x13 = 001 0011，R:0x63=011 0011
  //   contents of rom_1 (hex, n*v repeats v):
  //   1001 1401 1601 1081 1481 1581 1101 1201 1281 1681 1301 1381 41 41 41 1041 10c1 1141 1241 12c1 16c1
  //   1341 13c1 842 842 842 4*64 74 74 1067 17c7 2069 2041
  //   ROM FOR CONTROL LOGIC
  //   UType
  //   I3Type
  //   DON'T CHANGE THE LOCATIONS OF THE INPUTS AND OUTPUTS!
  //   This is only if you choose to do the ROM option
  //   CONNECT
  //   WIRE
  //   TO
  //   USE
  //   ROM
  //   OUTPUT from your circuit
  //   Reminder: If using ROM, use combinational logic for PCSel
endmodule
